// Logisim project Day_00.circ as structural Verilog: 1 circuit, main circuit main
module main (
  input  A,
  input  B
);

  wire G1_out;

  and G1 (G1_out, A, B);
  LED led_1 (.in(G1_out));
endmodule
